# Fritzing sketch Robot (saved by Fritzing 0.9.3b)

parts:
  Part3 = NRF24L01+ Breakout Board
  Part4 = Arduino Nano (Rev3.0)
  L298N1 = L298N DC motor driver
  U1 = SWITCH_SPDT [package=kps-1290]
  DC_Mot_Enc1 = DC Motor with two-phase hall-encoder [part_number=VT-E-G25A-06-177E]
  DC_Mot_Enc2 = DC Motor with two-phase hall-encoder [part_number=VT-E-G25A-06-177E]
  BAT1 = 12 battery [package=battery]

nets:
  GND: Part3.GND, Part4.GND, DC_Mot_Enc1.pin2
  VCC: Part3.VCC, Part4.3V3
  N1: Part3.CE, Part4.D7
  N2: Part3.CS, Part4.D8
  N3: Part3.SCK, Part4.D13/SCK
  N4: Part3.MOSI, Part4.D11/MOSI
  N5: Part3.MISO, Part4.D12/MISO
  N6: Part4.D2, DC_Mot_Enc1.pin4
  N7: Part4.D3, DC_Mot_Enc2.pin4
  N8: Part4.D4, L298N1.ENB
  N9: Part4.D5, L298N1.ENA
  N10: Part4.D9, DC_Mot_Enc1.pin3
  N11: Part4.D10, DC_Mot_Enc2.pin3
  VIN: Part4.VIN, L298N1.5V
  N12: Part4.A3, L298N1.IN4
  N13: Part4.A2, L298N1.IN3
  N14: Part4.A1, L298N1.IN2
  N15: Part4.A0, L298N1.IN1
  N16: L298N1.OUT1, DC_Mot_Enc1.pin6
  N17: L298N1.OUT2, DC_Mot_Enc1.pin1
  N18: L298N1.OUT3, DC_Mot_Enc2.pin6
  N19: L298N1.OUT4, DC_Mot_Enc2.pin1
  N20: L298N1.12V, U1.S
  N21: L298N1.GND, BAT1.-
  N22: U1.O, BAT1.+

custom parts:
  L298N DC motor driver: 2x DC motor driver with 78M05 positive voltage regulator (7..35 V) L298N: max 46 V, 2 A Set 5 V Enable jumper to enable 5 V regultor (needed for the L298N) and +5 V output at screw terminal or supply external +5 V at screw terminal Set ENA and/or ENB to +5 V to enable motor permanently or supply ENA and/or ENB with PWM signal IN1 and IN2 set rotation directory for motor A (OUT1/OUT2) IN2 and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
  12 battery: 12V lead acid type battery, like the Husqvarna YTH2448 12V 35AH battery. This is the mini version 1/4 the size of the actual battery to be closer to typical breadboard parts (around 2in wide rathher than 7in). The pads in pcb are sized to accomidate up to 14ga wire (as these batterys will deliver high currents.)
